# Fritzing sketch circuit (saved by Fritzing 0.7.10b)
breadboards: 1

parts:
  Part1 = Bluetooth Mate Silver
  Arduino = Arduino
  LED = LED - 5mm [color="Red (633nm)" package="5 mm [THT]"]
  Potentiometer = Rotary Potentiometer (Small) [maximum_resistance=100kΩ]

nets:
  N1: Part1.RTS_5V, Part1.CTS_5V
  N2: Part1.RX_5V, Arduino.D1TX
  N3: Part1.TX_5V, Arduino.D0RX
  VCC: Part1.VCC, Arduino.+5V, Potentiometer.leg2
  GND: Part1.GND, Arduino.GND, LED.cathode, Potentiometer.leg1
  N4: Arduino.D13, LED.anode
  N5: Arduino.A0, Potentiometer.wiper
